# Fritzing sketch EVImk1 (saved by Fritzing 0.8.7b)
breadboards: 3

parts:
  Part2 = Adafruit MPR121
  Part5 = Arduino Mega 2560 (Rev3)
  Part6 = Adafruit MPR121
  Part7 = Arduino Nano (Rev3.0)
  MPX5010GP = MPX4250AP pressure sensor [part_number=MPX]
  S1 = Toggle Switch [package=THT]
  U1 = POT [package=alps_pot]
  C1 = Electrolytic Capacitor [capacitance=1µF package="100 mil [THT, electrolytic]"]
  DIN1 = DIN-5 jack (MIDI) [package=THT]
  R1 = Resistor [tolerance=±5% resistance=220 package=THT]
  R2 = Resistor [tolerance=±5% resistance=220 package=THT]
  J1 = Basic Force Sensing Resistor (FSR) [package=THT]
  R3 = Resistor [tolerance=±5% resistance=1k package=THT]
  S2 = Pushbutton [package="[THT]"]
  S3 = Pushbutton [package="[THT]"]
  S4 = Pushbutton [package="[THT]"]
  Part8 = Black Joystick KY-023
  Part4 = Bicolor 8x8 LED Matrix Backpack [part_number=902]
  J2 = female pin header, 2 pins [form="♀ (female)"]
  J3 = female pin header, 2 pins [form="♀ (female)"]
  J4 = female pin header, 2 pins [form="♀ (female)"]
  J5 = female pin header, 2 pins [form="♀ (female)"]
  J6 = female pin header, 2 pins [form="♀ (female)"]
  J7 = female pin header, 2 pins [form="♀ (female)"]
  J8 = female pin header, 2 pins [form="♀ (female)"]
  J9 = female pin header, 2 pins [form="♀ (female)"]
  J10 = female pin header, 2 pins [form="♀ (female)"]
  J11 = female pin header, 2 pins [form="♀ (female)"]
  J12 = female pin header, 2 pins [form="♀ (female)"]
  J13 = female pin header, 2 pins [form="♀ (female)"]
  J14 = female pin header, 2 pins [form="♀ (female)"]
  J15 = female pin header, 2 pins [form="♀ (female)"]
  J16 = female pin header, 2 pins [form="♀ (female)"]
  R4 = Resistor [tolerance=±5% resistance=10M package=THT]
  R5 = Resistor [tolerance=±5% resistance=10M package=THT]
  J17 = female pin header, 2 pins [form="♀ (female)"]
  J18 = female pin header, 2 pins [form="♀ (female)"]
  Part9 = Arduino Nano (Rev3.0)
  Part10 = Arduino Mega 2560 (Rev3)
  Part11 = I2C Non-Volatile FRAM 32KB
  Part12 = OLED Monochrome 128x64 1.3 inch [part_number=938]
  Part13 = Black Joystick KY-023
  S5 = Pushbutton [package="[THT]"]
  S6 = Pushbutton [package="[THT]"]

nets:
  N1: Part2.ELEC6, J2.pin1
  N2: Part2.ELEC5, J3.pin1
  N3: Part2.ELEC4, J4.pin1
  N4: Part2.ELEC3, J6.pin1
  N5: Part2.ELEC2, J5.pin1
  N6: Part2.ELEC1, J7.pin1
  N7: Part2.ELEC0, J10.pin1
  GND: Part2.GND, Part5.GND, Part6.GND, Part7.GND, MPX5010GP.GND, U1.A, C1.+, DIN1.2, R3.Pin_0, S2.Pin_3, S2.Pin_4, S3.Pin_3, S3.Pin_4, S4.Pin_3, S4.Pin_4, Part8.GND, Part4.GND, Part9.GND
  VIN: Part2.VIN, Part5.5V, Part6.VIN, MPX5010GP.Vs, U1.E, C1.-, R1.Pin_1, J1.pin_0, Part8.+5V, Part4.VDD
  N8: Part2.3.3V, Part2.ADDR
  N9: Part2.SDA, Part5.D20/SDA, Part5.SDA, Part6.SDA, Part4.SDA
  N10: Part2.SCL, Part5.D21/SCL, Part5.SCL, Part6.SCL, Part4.SCL
  N11: Part5.A0, MPX5010GP.V_out
  N12: Part5.A1, U1.S
  N13: Part5.A2, J1.pin_1, R3.Pin_1
  N14: Part5.D17_PWM/RX2, Part7.D0/RX, Part9.D0/RX
  N15: Part5.VIN, S1.L1
  N16: Part5.D1_TX0, R2.Pin_0
  N17: Part5.D2_PWM, S2.Pin_1
  N18: Part5.D3_PWM, S3.Pin_1
  N19: Part5.D4_PWM, S4.Pin_1
  N20: Part5.D5_PWM, Part8.SW
  N21: Part6.ELEC11, J11.pin1
  N22: Part6.ELEC10, J12.pin1
  N23: Part6.ELEC9, J13.pin1
  N24: Part6.ELEC8, J14.pin1
  N25: Part6.ELEC7, J15.pin1
  N26: Part6.ELEC6, J16.pin1
  N27: Part6.ELEC5, J9.pin1
  N28: Part6.ELEC4, J8.pin1
  N29: Part7.D1/TX, Part9.D1/TX
  N30: Part7.RESET, Part9.RESET
  N31: Part7.D2, R4.Pin_1, R5.Pin_1, Part9.D2
  N32: Part7.D3, J17.pin2, Part9.D3
  N33: Part7.D4, J18.pin2, Part9.D4
  N34: Part7.D5, Part9.D5
  N35: Part7.D6, Part9.D6
  N36: Part7.D7, Part9.D7
  N37: Part7.D8, Part9.D8
  N38: Part7.D9, Part9.D9
  N39: Part7.D10, Part9.D10
  N40: Part7.D11/MOSI, Part9.D11/MOSI
  N41: Part7.D12/MISO, Part9.D12/MISO
  VIN_2: Part7.VIN, S1.COM, Part9.VIN
  5V: Part7.5V, Part9.5V
  N42: Part7.A7, Part9.A7
  N43: Part7.A6, Part9.A6
  N44: Part7.A5, Part9.A5
  N45: Part7.A4, Part9.A4
  N46: Part7.A3, Part9.A3
  N47: Part7.A2, Part9.A2
  N48: Part7.A1, Part9.A1
  N49: Part7.A0, Part9.A0
  N50: Part7.AREF, Part9.AREF
  3V3: Part7.3V3, Part9.3V3
  N51: Part7.D13/SCK, Part9.D13/SCK
  N52: DIN1.5, R1.Pin_0
  N53: DIN1.4, R2.Pin_1
  N54: R4.Pin_0, J17.pin1
  N55: R5.Pin_0, J18.pin1
  N56: Part10.A0, Part13.VRy
  N57: Part10.A1, Part13.VRx
  N58: Part10.SCL, Part11.SCL
  N59: Part10.SDA, Part11.SDA
  N60: Part10.D13_PWM, Part12.CS
  N61: Part10.D12_PWM, Part12.RESET
  N62: Part10.D11_PWM, Part12.DC_SA0
  N63: Part10.D10_PWM, Part12.SCLK_SCK
  N64: Part10.D9_PWM, Part12.MOSI_SDA
  5V_2: Part10.5V, Part11.VCC, Part12.VIN, Part13.+5V
  GND_2: Part10.GND, Part11.GND, Part12.GND, Part13.GND, S5.Pin_1, S5.Pin_2, S6.Pin_1, S6.Pin_2
  N65: Part10.D2_PWM, S5.Pin_3, S5.Pin_4
  N66: Part10.D3_PWM, S6.Pin_3, S6.Pin_4

notes:
  Pitch Bend Down Pad
  Pitch Bend Up Pad
  Trill Vave 3 (+4)
  Trill Vave 2 (+1)
  Trill Vave 1 (+2)
  Valve 3 (-3)
  Valve 2 (-1)
  Valve 1 (-2)
  Partial Valve (-5)
  Multiphonics Button
  Multiphonics Off
  Octave 1 (+12)
  Partial Valve
  Octave 2 (+24)
  Octave 6 (+72)
  Octave 4 (+48)
  Octave 3 (+36)
  Octave 5 (+60)

custom parts:
  Adafruit MPR121: Add lots of touch sensors to your next microcontroller project with this easy-to-use 12-channel capacitive touch sensor breakout board, starring the MPR121. This chip can handle up to 12 individual touch pads. The MPR121 has support for only I2C, which can be implemented with nearly any microcontroller. You can select one of 4 addresses with the ADDR pin, for a total of 48 capacitive touch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
  Black Joystick KY-023: Description: The joystick is a combination of 2 analoog potentiometer and a digital switch. Arduino GND --> Module pin - Arduino +5V --> Module pin +5V Arduino Analoog 0 --> Module VRx Arduino Analoog 1 --> Module VRy Arduino Digital --> Module SW Dimensions: 1" x 1.25"
  Bicolor 8x8 LED Matrix Backpack: This 1.2" bi-color 8x8 LED matrix includes a driver chip for simple control via an I2C interface. It's called a Bicolor LED, but you can have 3 colors total by turning on the red and green LEDs, which creates yellow. That's 3 colors for the price of 2! The backpacks come with address-selection jumpers so you can connect up to eight bicolor matrices on a single I2C bus.
  I2C Non-Volatile FRAM 32KB: With our I2C FRAM breakout board you can add some FRAM storage to your next DIY project. FRAM allows for a lower power usage and a faster write performance. It's excellent for low-power or inconsistent-power datalogging or data buffering where you want to stream data fast while also keeping the data when there's no power. Unlike Flash or EEPROM there's no pages to worry about. Each byte can be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
  OLED Monochrome 128x64 1.3 inch: These displays are small, only about 1.3" diagonal, but very readable due to the high contrast of an OLED display. This display is made of 128x64 individual white OLED pixels, each one is turned on or off by the controller chip. Because the display makes its own light, no backlight is required. This reduces the power required to run the OLED and is why the display has such high contrast; we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
