# Fritzing sketch EVImk2v2 (saved by Fritzing 0.8.7b)
stripboards: 2
perfboards: 20

parts:
  Part2 = Adafruit MPR121  # not connected
  Part6 = Adafruit MPR121  # not connected
  MPX5010GP = MPX4250AP pressure sensor [part_number=MPX]  # not connected
  U1 = POT [package=alps_pot]  # not connected
  DIN1 = DIN-5 jack (MIDI) [package=THT]  # not connected
  S2 = Pushbutton [package="[THT]"]  # not connected
  S3 = Pushbutton [package="[THT]"]  # not connected
  S4 = Pushbutton [package="[THT]"]  # not connected
  Part4 = Bicolor 8x8 LED Matrix Backpack [part_number=902]  # not connected
  Part11 = I2C Non-Volatile FRAM 32KB  # not connected
  Part12 = OLED Monochrome 128x64 1.3 inch [part_number=938]  # not connected
  Part13 = Black Joystick KY-023  # not connected
  S6 = Pushbutton [package="[THT]"]  # not connected
  Teensy1 = Teensy 3.6 (Basic)
  U2 = LM 358 Dual Op-Amp [package="DIP8 [THT]"]  # not connected
  R1 = Resistor [tolerance=±5% resistance=3.3k package=THT]  # not connected
  R2 = Resistor [tolerance=±5% resistance=1M package=THT]  # not connected
  R3 = Resistor [tolerance=±5% resistance=1M package=THT]  # not connected
  R4 = Resistor [tolerance=±5% resistance=1M package=THT]  # not connected
  R5 = Resistor [tolerance=±5% resistance=220 package=THT]  # not connected
  R6 = Resistor [tolerance=±5% resistance=220 package=THT]  # not connected
  C1 = Electrolytic Capacitor [capacitance=1µF package="100 mil [THT, electrolytic]"]  # not connected
  C2 = Electrolytic Capacitor [capacitance=1µF package="100 mil [THT, electrolytic]"]  # not connected
  C3 = Electrolytic Capacitor [capacitance=1µF package="100 mil [THT, electrolytic]"]  # not connected
  C4 = Electrolytic Capacitor [capacitance=1µF package="100 mil [THT, electrolytic]"]  # not connected
  C5 = Electrolytic Capacitor [capacitance=1µF package="100 mil [THT, electrolytic]"]  # not connected
  C6 = Electrolytic Capacitor [capacitance=1µF package="100 mil [THT, electrolytic]"]  # not connected
  C7 = Electrolytic Capacitor [capacitance=1µF package="100 mil [THT, electrolytic]"]  # not connected
  C8 = Electrolytic Capacitor [capacitance=1µF package="100 mil [THT, electrolytic]"]  # not connected
  C9 = Electrolytic Capacitor [capacitance=1µF package="100 mil [THT, electrolytic]"]  # not connected

nets:
  GND: Teensy1.GND, Teensy1.GND1
  N1: Teensy1.3V3, Teensy1.3V3_1

notes:
  Partial Valve
  Valve 1 (-2)
  Valve 2 (-1)
  Valve 3 (-3)
  Trill Valve 1 (+2)
  Trill Valve 3 (+4)
  Trill Valve 2 (+1)
  Multiphonics Off
  Multiphonics Valve
  Pitch Bend Up
  Pitch Bend Down
  Octave Sensor 7 (+72)
  Octave Sensor 5 (+60)
  Octave Sensor 4 (+48)
  Octave Sensor 3 (+36)
  Octave Sensor 2 (+24)
  Octave Sensor 1 (+12)
  Partial Valve (-5)
  Extra Mod Sensor
  Bite Sensor

custom parts:
  Adafruit MPR121: Add lots of touch sensors to your next microcontroller project with this easy-to-use 12-channel capacitive touch sensor breakout board, starring the MPR121. This chip can handle up to 12 individual touch pads. The MPR121 has support for only I2C, which can be implemented with nearly any microcontroller. You can select one of 4 addresses with the ADDR pin, for a total of 48 capacitive touch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
  Bicolor 8x8 LED Matrix Backpack: This 1.2" bi-color 8x8 LED matrix includes a driver chip for simple control via an I2C interface. It's called a Bicolor LED, but you can have 3 colors total by turning on the red and green LEDs, which creates yellow. That's 3 colors for the price of 2! The backpacks come with address-selection jumpers so you can connect up to eight bicolor matrices on a single I2C bus.
  I2C Non-Volatile FRAM 32KB: With our I2C FRAM breakout board you can add some FRAM storage to your next DIY project. FRAM allows for a lower power usage and a faster write performance. It's excellent for low-power or inconsistent-power datalogging or data buffering where you want to stream data fast while also keeping the data when there's no power. Unlike Flash or EEPROM there's no pages to worry about. Each byte can be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
  OLED Monochrome 128x64 1.3 inch: These displays are small, only about 1.3" diagonal, but very readable due to the high contrast of an OLED display. This display is made of 128x64 individual white OLED pixels, each one is turned on or off by the controller chip. Because the display makes its own light, no backlight is required. This reduces the power required to run the OLED and is why the display has such high contrast; we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
  Black Joystick KY-023: Description: The joystick is a combination of 2 analoog potentiometer and a digital switch. Arduino GND --> Module pin - Arduino +5V --> Module pin +5V Arduino Analoog 0 --> Module VRx Arduino Analoog 1 --> Module VRy Arduino Digital --> Module SW Dimensions: 1" x 1.25"
  Teensy 3.6 (Basic): The Teensy is a complete USB-based microcontoller development system, in a very small footprint, capable of implementing many types of projects. All programming is done via the USB port. No special programmer is needed, only a standard micro-USB cable and a PC or Macintosh with a USB port.
