# Fritzing sketch EVImk3 (saved by Fritzing 0.8.7b)
breadboards: 1

parts:
  ATtiny45 = ATTINY45 [package=dip]
  Comparator = IC, DIP package, 8 pins [chip_label=Comparator]
  U2 = Mpxv5004dp [package=SOP]
  LED1 = LED - 5mm [color="Red (633nm)" package="5 mm [THT]"]
  Part1 = Adafruit MCP4725 Breakout Board - 12-Bit DAC [part_number="Adafruit #935"]
  R1 = Resistor [tolerance=±5% resistance=220 package=THT]
  breakout = female pin header, 5 pins [form="♀ (female)"]

nets:
  N1: ATtiny45.PB3(ADC3), Comparator.pin3, U2.OUT, breakout.pin3
  N2: ATtiny45.PB4(ADC2), breakout.pin5
  GND: ATtiny45.GND, Comparator.pin4, U2.GND, Part1.GND, R1.Pin_1, breakout.pin2
  N3: ATtiny45.PB0(MOSI), Part1.SDA
  N4: ATtiny45.PB2(SCK_ADC1), Part1.SCL
  VCC: ATtiny45.VCC, Comparator.pin8, U2.Vs, Part1.VDD, breakout.pin1
  N5: Comparator.pin1, LED1.anode, breakout.pin4
  N6: Comparator.pin2, Part1.VOUT
  N7: LED1.cathode, R1.Pin_0

custom parts:
  Mpxv5004dp: Mpxv5004dp pressure sensor
  Adafruit MCP4725 Breakout Board - 12-Bit DAC: Your microcontroller probably has an ADC (analog -> digital converter) but does it have a DAC (digital -> analog converter)??? Now it can! This breakout board features the easy-to-use MCP4725 12-bit DAC. Control it via I2C and send it the value you want it to output, and the VOUT pin will have it. Great for audio / analog projects, such as when you can't use PWM but need a sine wave or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
